# Fritzing sketch non-contact water detect (saved by Fritzing 0.9.3b)
circuit board: 4cm x 6cm
perfboards: 1

parts:
  Esp32_DevKit = DOIT Esp32 DevKit v1 (30 pins long, 11 pins width) [part_number=ESP32S-PIN30]
  part = Resistor [tolerance=±5% resistance=220 package=THT]
  part_2 = Resistor [tolerance=±5% resistance=220 package=THT]
  part_3 = Resistor [tolerance=±5% resistance=220 package=THT]
  LED = RGB LED (com. anode, rbg) [package="5 mm [THT]"]
  Water_sensor = male pin header, 4 pins [form="♂ (male)"]
  switch = SWITCH-SPST-2 [package=switch-spst-vertical]
  Buzzer1 = Buzzer 12mm [package=buzzer-12mm-ns-kit]
  pull_up = Resistor [tolerance=±5% resistance=1M package=THT]

nets:
  N1: Esp32_DevKit.GND, LED.common_anode, Water_sensor.pin3, Buzzer1.2
  N2: Esp32_DevKit.D4, Buzzer1.1
  N3: Esp32_DevKit.D34, part.Pin_0
  N4: Esp32_DevKit.D35, part_2.Pin_0
  N5: Esp32_DevKit.D32, part_3.Pin_0
  N6: Esp32_DevKit.D27, Water_sensor.pin2
  N7: Esp32_DevKit.D14, Water_sensor.pin4
  N8: Esp32_DevKit.D12, pull_up.Pin_0
  N9: Esp32_DevKit.VIN, switch.P, pull_up.Pin_1
  N10: part.Pin_1, LED.red_cathode
  N11: part_2.Pin_1, LED.blue_cathode
  N12: part_3.Pin_1, LED.green_cathode
  N13: Water_sensor.pin1, switch.O

custom parts:
  DOIT Esp32 DevKit v1 (30 pins long, 11 pins width): The DOIT Esp32 DevKit v1 is one of the development board created by DOIT to evaluate the ESP-WROOM-32 module. It is based on the ESP32 microcontroller that boasts Wifi, Bluetooth, Ethernet and Low Power support all in a single chip. (vanepp) made breadboard work, adjusted pin numbering and labels and reduced size of schematic and cleaned up pcb. This chip is 30pins long (2 x15) and 11 pins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
